# Fritzing sketch pad (saved by Fritzing 0.9.3b)

parts:
  Part1 = Arduino Micro (Rev3)
  U1 = SLIDER [package=slider]
  U2 = SLIDER [package=slider]
  U3 = SLIDER [package=slider]

nets:
  N1: Part1.GND, U1.E, U2.E, U3.E
  N2: Part1.5V, U1.A, U2.A, U3.A
